// Logisim project Trabalho Arquitetura CC3MB Felipe.circ as structural Verilog: 16 circuits, main circuit main
module main (
);

  wire clock_1_out, d_ff_1_q, d_ff_2_q, not_1_out, not_2_out, Reset_out, uc_1_clk_ac, uc_1_clk_pc,
       uc_1_clk_ram, uc_1_clk_rl, \uc_1_direção , uc_1_e, uc_1_load, uc_1_r_w, uc_1_rst_pc, ula_1_overflow,
       ula_1_zero;
  wire [2:0] \uc_1_operação ;
  wire [3:0] mux2x1_1_s, PC_q, ram_1_data, reg_ac_1_q, \uc_1_b_endereços , uc_1_dados, uc_1_operando, ula_1_s;
  wire [7:0] ir_1_q, rom_1_data;

  ROM #(.addrWidth(4)) rom_1 (.addr(PC_q), .data(rom_1_data));  // open: sel
  Counter #(.width(4), .max('hf), .trigger("falling")) PC (
    .load(uc_1_load), .D(uc_1_dados), .count(not_1_out), .Q(PC_q), .clk(uc_1_clk_pc), .clr(uc_1_rst_pc));  // open: carry
  not not_1 (not_1_out, uc_1_load);
  UC uc_1 (
    .\B_Endereços (\uc_1_b_endereços ), .Operando(uc_1_operando), .\Direção (\uc_1_direção ), .E(uc_1_e),
    .\Operação (\uc_1_operação ), .\Instrução (ir_1_q), .Clock(clock_1_out), .Reset(Reset_out),
    .RST_PC(uc_1_rst_pc), .clk_RL(uc_1_clk_rl), .clk_PC(uc_1_clk_pc), .clk_AC(uc_1_clk_ac),
    .clk_RAM(uc_1_clk_ram), .Zero(d_ff_2_q), .Load(uc_1_load), .Overflow(d_ff_1_q), .Dados(uc_1_dados),
    .R_W(uc_1_r_w));
  Button Reset (.out(Reset_out));
  Clock clock_1 (.out(clock_1_out));
  // Probe on ir_1_q
  IR ir_1 (.Clock(uc_1_clk_rl), .D(rom_1_data), .Q(ir_1_q));
  // Probe on reg_ac_1_q
  MUX2x1 mux2x1_1 (.Controle(\uc_1_direção ), .in_1(uc_1_operando), .in_2(ram_1_data), .S(mux2x1_1_s));
  ULA ula_1 (
    .D(uc_1_e), .A(reg_ac_1_q), .B(mux2x1_1_s), .\Operações (\uc_1_operação ), .Zero(ula_1_zero),
    .Overflow(ula_1_overflow), .S(ula_1_s));
  REG_AC reg_ac_1 (.Clock(uc_1_clk_ac), .D(ula_1_s), .Q(reg_ac_1_q));
  // Probe on mux2x1_1_s
  // Probe on reg_ac_1_q
  not not_2 (not_2_out, uc_1_r_w);
  D_Flip_Flop d_ff_1 (.clk(uc_1_clk_ac), .D(ula_1_overflow), .Q(d_ff_1_q));  // open: Qn, preset, en, reset
  D_Flip_Flop d_ff_2 (.clk(uc_1_clk_ac), .D(ula_1_zero), .Q(d_ff_2_q));  // open: Qn, preset, en, reset
  RAM #(.addrWidth(4), .dataWidth(4)) ram_1 (
    .addr(\uc_1_b_endereços ), .data(ram_1_data), .clk(uc_1_clk_ram), .ld(uc_1_r_w));  // open: sel, clr
  Buffer buffer_1 (.B(reg_ac_1_q), .in_2(not_2_out), .S(ram_1_data));

  // Notes on the sheet:
  //   0
  //   MOV
  //   1
  //   MOV
  //   ADD
  //   2
  //   3
  //   ADD
  //   SUB
  //   4
  //   5
  //   SUB
  //   6
  //   OR
  //   OR
  //   7
  //   8
  //   NOT
  //   NOT
  //   9
  //   A
  //   SHF
  //   SHF
  //   B
  //   JPZ
  //   C
  //   JPO
  //   D
  //   GO
  //   E
  //   STR
  //   F
  //   Instruction Set
  //   0
  //   000
  //   AC <= X
  //   1
  //   AC <= M(X)
  //   000
  //   0
  //   AC <= AC+X
  //   001
  //   1
  //   001
  //   AC <= AC+M(X)
  //   0
  //   010
  //   AC <= AC-X
  //   010
  //   1
  //   AC <= AC-M(X)
  //   0
  //   011
  //   1
  //   011
  //   0
  //   100
  //   AC <= NOT X
  //   100
  //   1
  //   0
  //   101
  //   AC <= AC << Q
  //   1
  //   101
  //   AC <= AC >> Q
  //   0
  //   110
  //   110
  //   1
  //   PC <= X
  //   0
  //   111
  //   1
  //   M(X) <= AC 
  //   111
  //   AC <= AC OR X
  //   AC <= AC OR M(X)
  //   AC <= NOT M( X)
  //   PC <= X SE FLAG Z
  //   PC <= X SE FLAG O
  //   contents of rom_1 (hex, n*v repeats v):
  //   0 f0 1 f1 10 31 d0 f2 11 f0 12 f1 e4
endmodule

module ADD_1 (
  input  A,
  input  B,
  input  Vem_1,
  output S,
  output Vai_1
);

  wire and_1_out, and_2_out, or_1_out, xor_1_out;

  xor xor_1 (xor_1_out, A, B);
  or or_1 (or_1_out, B, Vem_1);
  and and_1 (and_1_out, B, Vem_1);
  xor xor_2 (S, xor_1_out, Vem_1);
  and and_2 (and_2_out, or_1_out, A);
  or or_2 (Vai_1, and_2_out, and_1_out);
endmodule

module ADD_4 (
  input  [3:0] in_1,
  input  [3:0] in_2,
  input  Vem_1,
  output Vai_1,
  output [3:0] out_5
);

  wire add_1_2_vai_1, add_1_3_vai_1, add_1_4_vai_1;

  ADD_1 add_1_1 (.A(in_1[3]), .B(in_2[3]), .Vem_1(add_1_2_vai_1), .S(out_5[3]), .Vai_1(Vai_1));
  ADD_1 add_1_2 (.A(in_1[2]), .B(in_2[2]), .Vem_1(add_1_3_vai_1), .S(out_5[2]), .Vai_1(add_1_2_vai_1));
  ADD_1 add_1_3 (.A(in_1[1]), .B(in_2[1]), .Vem_1(add_1_4_vai_1), .S(out_5[1]), .Vai_1(add_1_3_vai_1));
  ADD_1 add_1_4 (.A(in_1[0]), .B(in_2[0]), .Vem_1(Vem_1), .S(out_5[0]), .Vai_1(add_1_4_vai_1));
endmodule

module SUB_1 (
  input  A,
  input  B,
  input  Vem_1,
  output S,
  output Vai_1
);

  wire and_1_out, and_2_out, not_1_out, or_1_out, xor_1_out;

  not not_1 (not_1_out, A);
  xor xor_1 (xor_1_out, A, B);
  or or_1 (or_1_out, B, Vem_1);
  and and_1 (and_1_out, B, Vem_1);
  xor xor_2 (S, xor_1_out, Vem_1);
  and and_2 (and_2_out, or_1_out, not_1_out);
  or or_2 (Vai_1, and_2_out, and_1_out);
endmodule

module SUB_4 (
  input  [3:0] in_1,
  input  [3:0] in_2,
  input  Vem_1,
  output Overflow,
  output [3:0] out_5
);

  wire sub_1_2_vai_1, sub_1_3_vai_1, sub_1_4_vai_1;

  SUB_1 sub_1_1 (.A(in_1[3]), .B(in_2[3]), .Vem_1(sub_1_2_vai_1), .S(out_5[3]), .Vai_1(Overflow));
  SUB_1 sub_1_2 (.A(in_1[2]), .B(in_2[2]), .Vem_1(sub_1_3_vai_1), .S(out_5[2]), .Vai_1(sub_1_2_vai_1));
  SUB_1 sub_1_3 (.A(in_1[1]), .B(in_2[1]), .Vem_1(sub_1_4_vai_1), .S(out_5[1]), .Vai_1(sub_1_3_vai_1));
  SUB_1 sub_1_4 (.A(in_1[0]), .B(in_2[0]), .Vem_1(Vem_1), .S(out_5[0]), .Vai_1(sub_1_4_vai_1));
endmodule

module Buffer (
  input  [3:0] B,
  input  in_2,
  output [3:0] S
);

  assign S[3] = in_2 ? B[3] : 1'bz;  // Controlled_Buffer controlled_buffer_1
  assign S[2] = in_2 ? B[2] : 1'bz;  // Controlled_Buffer controlled_buffer_2
  assign S[1] = in_2 ? B[1] : 1'bz;  // Controlled_Buffer controlled_buffer_3
  assign S[0] = in_2 ? B[0] : 1'bz;  // Controlled_Buffer controlled_buffer_4
endmodule

module Decoder (
  input  [2:0] \Operação ,
  output S0,
  output S1,
  output S2,
  output S3,
  output S4,
  output S5,
  output S6,
  output S7
);

  wire not_1_out, not_2_out, not_3_out, not_4_out, not_5_out, not_6_out, not_7_out, not_8_out, not_9_out,
       not_10_out, not_11_out, not_12_out;

  not not_1 (not_1_out, \Operação [2]);
  not not_2 (not_2_out, \Operação [1]);
  not not_3 (not_3_out, \Operação [0]);
  not not_4 (not_4_out, \Operação [2]);
  not not_5 (not_5_out, \Operação [1]);
  not not_6 (not_6_out, \Operação [2]);
  not not_7 (not_7_out, \Operação [0]);
  not not_8 (not_8_out, \Operação [2]);
  not not_9 (not_9_out, \Operação [1]);
  not not_10 (not_10_out, \Operação [0]);
  not not_11 (not_11_out, \Operação [1]);
  not not_12 (not_12_out, \Operação [0]);
  and and_1 (S0, not_1_out, not_2_out, not_3_out);
  and and_2 (S1, not_4_out, not_5_out, \Operação [0]);
  and and_3 (S2, not_6_out, \Operação [1], not_7_out);
  and and_4 (S3, not_8_out, \Operação [1], \Operação [0]);
  and and_5 (S4, \Operação [2], not_9_out, not_10_out);
  and and_6 (S5, \Operação [2], not_11_out, \Operação [0]);
  and and_7 (S6, \Operação [2], \Operação [1], not_12_out);
  and and_8 (S7, \Operação [2], \Operação [1], \Operação [0]);
endmodule

module Buffer_invertido (
  input  [3:0] B,
  input  in_2,
  output [3:0] S
);

  assign S[0] = in_2 ? ~B[3] : 1'bz;  // Controlled_Inverter controlled_inverter_1
  assign S[2] = in_2 ? ~B[1] : 1'bz;  // Controlled_Inverter controlled_inverter_2
  assign S[1] = in_2 ? ~B[2] : 1'bz;  // Controlled_Inverter controlled_inverter_3
  assign S[3] = in_2 ? ~B[0] : 1'bz;  // Controlled_Inverter controlled_inverter_4
endmodule

module ROT_L (
  input  [1:0] XY,
  input  [3:0] ABCD,
  output [3:0] abcd_2
);

  wire and_1_out, and_2_out, and_3_out, and_4_out, and_5_out, and_6_out, and_7_out, and_8_out, and_9_out;

  and and_1 (and_1_out, ~XY[1], ~XY[0], ABCD[3]);  // AND_Gate
  and and_2 (and_2_out, ~XY[1], XY[0], ABCD[2]);  // AND_Gate
  and and_3 (and_3_out, XY[1], ~XY[0], ABCD[1]);  // AND_Gate
  and and_4 (and_4_out, XY[1], XY[0], ABCD[0]);
  and and_5 (and_5_out, ~XY[1], ~XY[0], ABCD[2]);  // AND_Gate
  and and_6 (and_6_out, ~XY[1], XY[0], ABCD[1]);  // AND_Gate
  and and_7 (and_7_out, XY[1], ~XY[0], ABCD[0]);  // AND_Gate
  and and_8 (and_8_out, ~XY[1], ~XY[0], ABCD[1]);  // AND_Gate
  and and_9 (and_9_out, ~XY[1], XY[0], ABCD[0]);  // AND_Gate
  and and_10 (abcd_2[0], ~XY[1], ~XY[0], ABCD[0]);  // AND_Gate
  or or_1 (abcd_2[3], and_1_out, and_2_out, and_3_out, and_4_out);
  or or_2 (abcd_2[2], and_5_out, and_6_out, and_7_out);
  or or_3 (abcd_2[1], and_8_out, and_9_out);
endmodule

module ROT_D (
  input  [3:0] ABCD,
  input  [1:0] XY,
  output [3:0] abcd_2
);

  wire and_1_out, and_2_out, and_3_out, and_4_out, and_5_out, and_6_out, and_7_out, and_8_out, and_9_out;

  and and_1 (and_1_out, ~XY[1], ~XY[0], ABCD[0]);  // AND_Gate
  and and_2 (and_2_out, ~XY[1], XY[0], ABCD[1]);  // AND_Gate
  and and_3 (and_3_out, XY[1], ~XY[0], ABCD[2]);  // AND_Gate
  and and_4 (and_4_out, XY[1], XY[0], ABCD[3]);
  and and_5 (and_5_out, ~XY[1], ~XY[0], ABCD[1]);  // AND_Gate
  and and_6 (and_6_out, ~XY[1], XY[0], ABCD[2]);  // AND_Gate
  and and_7 (and_7_out, XY[1], ~XY[0], ABCD[3]);  // AND_Gate
  and and_8 (and_8_out, ~XY[1], ~XY[0], ABCD[2]);  // AND_Gate
  and and_9 (and_9_out, ~XY[1], XY[0], ABCD[3]);  // AND_Gate
  and and_10 (abcd_2[3], ~XY[1], ~XY[0], ABCD[3]);  // AND_Gate
  or or_1 (abcd_2[0], and_1_out, and_2_out, and_3_out, and_4_out);
  or or_2 (abcd_2[1], and_5_out, and_6_out, and_7_out);
  or or_3 (abcd_2[2], and_8_out, and_9_out);
endmodule

module OR_4_BITS (
  input  [3:0] B,
  input  [3:0] A,
  output [3:0] S
);

  or or_1 (S[3], A[3], B[3]);
  or or_2 (S[2], A[2], B[2]);
  or or_3 (S[0], A[0], B[0]);
  or or_4 (S[1], A[1], B[1]);
endmodule

module ULA (
  input  D,
  input  [3:0] A,
  input  [3:0] B,
  input  [2:0] \Operações ,
  output Overflow,
  output [3:0] S,
  output Zero
);

  wire add_4_1_vai_1, and_1_out, and_2_out, decoder_1_s0, decoder_1_s1, decoder_1_s2, decoder_1_s3,
       decoder_1_s4, decoder_1_s5, decoder_1_s6, decoder_1_s7, not_1_out, sub_4_1_overflow;
  wire [3:0] add_4_1_out_5, buffer_5_s, or_4_bits_1_s, rot_d_1_abcd_2, rot_l_1_abcd_2, sub_4_1_out_5;

  or or_1 (Overflow, and_1_out, and_2_out);
  and and_1 (and_1_out, add_4_1_vai_1, decoder_1_s1);
  and and_2 (and_2_out, sub_4_1_overflow, decoder_1_s2);
  Decoder decoder_1 (
    .\Operação (\Operações ), .S0(decoder_1_s0), .S1(decoder_1_s1), .S2(decoder_1_s2), .S3(decoder_1_s3),
    .S4(decoder_1_s4), .S5(decoder_1_s5), .S6(decoder_1_s6), .S7(decoder_1_s7));
  nor nor_1 (Zero, decoder_1_s7, decoder_1_s6, S[0], S[1], S[2], S[3]);
  Buffer buffer_1 (.B(B), .in_2(decoder_1_s0), .S(S));
  ADD_4 add_4_1 (.in_1(A), .Vai_1(add_4_1_vai_1), .in_2(B), .Vem_1(1'b0), .out_5(add_4_1_out_5));
  Buffer buffer_2 (.B(add_4_1_out_5), .in_2(decoder_1_s1), .S(S));
  SUB_4 sub_4_1 (.in_1(A), .Overflow(sub_4_1_overflow), .in_2(B), .Vem_1(1'b0), .out_5(sub_4_1_out_5));
  Buffer buffer_3 (.B(sub_4_1_out_5), .in_2(decoder_1_s2), .S(S));
  OR_4_BITS or_4_bits_1 (.A(A), .B(B), .S(or_4_bits_1_s));
  Buffer buffer_4 (.B(or_4_bits_1_s), .in_2(decoder_1_s3), .S(S));
  // Buffer_invertido buffer_invertido_1: pin names not known; wires that end beside it: B, decoder_1_s4, S
  ROT_D rot_d_1 (.abcd_2(rot_d_1_abcd_2), .ABCD(A), .XY(B[1:0]));
  ROT_L rot_l_1 (.abcd_2(rot_l_1_abcd_2), .ABCD(A), .XY(B[1:0]));
  not not_1 (not_1_out, D);
  Buffer buffer_5 (.B(rot_l_1_abcd_2), .in_2(not_1_out), .S(buffer_5_s));
  Buffer buffer_6 (.B(rot_d_1_abcd_2), .in_2(D), .S(buffer_5_s));
  Buffer buffer_7 (.B(buffer_5_s), .in_2(decoder_1_s5), .S(S));
endmodule

module REG_AC (
  input  Clock,
  input  [3:0] D,
  output [3:0] Q
);

  D_Flip_Flop D3 (.clk(Clock), .D(D[3]), .Q(Q[3]));  // open: Qn, preset, en, reset
  D_Flip_Flop D2 (.clk(Clock), .D(D[2]), .Q(Q[2]));  // open: Qn, preset, en, reset
  D_Flip_Flop D1 (.clk(Clock), .D(D[1]), .Q(Q[1]));  // open: Qn, preset, en, reset
  D_Flip_Flop D0 (.clk(Clock), .D(D[0]), .Q(Q[0]));  // open: Qn, preset, en, reset
endmodule

module MUX2x1 (
  input  [3:0] in_1,
  input  [3:0] in_2,
  input  Controle,
  output [3:0] S
);

  wire not_1_out;

  not not_1 (not_1_out, Controle);
  Buffer buffer_1 (.B(in_1), .in_2(not_1_out), .S(S));
  Buffer buffer_2 (.B(in_2), .in_2(Controle), .S(S));
endmodule

module IR (
  input  Clock,
  input  [7:0] D,
  output [7:0] Q
);

  D_Flip_Flop #(.trigger("falling")) d_ff_1 (.clk(Clock), .D(D[7]), .Q(Q[7]));  // open: Qn, preset, en, reset
  D_Flip_Flop #(.trigger("falling")) d_ff_2 (.clk(Clock), .D(D[6]), .Q(Q[6]));  // open: Qn, preset, en, reset
  D_Flip_Flop d_ff_3 (.clk(Clock), .D(D[5]), .Q(Q[5]));  // open: Qn, preset, en, reset
  D_Flip_Flop #(.trigger("falling")) d_ff_4 (.clk(Clock), .D(D[4]), .Q(Q[4]));  // open: Qn, preset, en, reset
  D_Flip_Flop #(.trigger("falling")) d_ff_5 (.clk(Clock), .D(D[3]), .Q(Q[3]));  // open: Qn, preset, en, reset
  D_Flip_Flop #(.trigger("falling")) d_ff_6 (.clk(Clock), .D(D[2]), .Q(Q[2]));  // open: Qn, preset, en, reset
  D_Flip_Flop #(.trigger("falling")) d_ff_7 (.clk(Clock), .D(D[1]), .Q(Q[1]));  // open: Qn, preset, en, reset
  D_Flip_Flop #(.trigger("falling")) d_ff_8 (.clk(Clock), .D(D[0]), .Q(Q[0]));  // open: Qn, preset, en, reset
endmodule

module UC (
  input  [7:0] \Instrução ,
  input  Clock,
  input  Reset,
  input  Overflow,
  input  Zero,
  output [3:0] Dados,
  output [3:0] \B_Endereços ,
  output [3:0] Operando,
  output clk_RL,
  output clk_RAM,
  output clk_AC,
  output \Direção ,
  output clk_PC,
  output RST_PC,
  output E,
  output [2:0] \Operação ,
  output R_W,
  output Load
);

  wire GoTo_out, JPO_out, JPZ_out, nand_1_out;
  wire [1:0] counter_1_q;

  nand Storage (R_W, \Instrução [7], \Instrução [6], \Instrução [5], \Instrução [4], clk_AC);
  Counter #(.width(2), .max('h3)) counter_1 (.Q(counter_1_q), .clk(Clock), .clr(Reset));  // open: load, D, count, carry
  and GoTo (GoTo_out, \Instrução [7], \Instrução [6], \Instrução [5], ~\Instrução [4], clk_PC);  // AND_Gate
  and and_1 (clk_RL, ~counter_1_q[0], ~counter_1_q[1]);  // AND_Gate
  and and_2 (clk_PC, counter_1_q[0], ~counter_1_q[1]);  // AND_Gate
  and JPO (JPO_out, \Instrução [7], \Instrução [6], ~\Instrução [5], \Instrução [4], clk_PC, Overflow);  // AND_Gate
  or or_1 (Load, GoTo_out, JPO_out, JPZ_out);
  and and_3 (clk_RAM, counter_1_q[0], counter_1_q[1]);
  and and_4 (clk_AC, ~counter_1_q[0], counter_1_q[1]);  // AND_Gate
  and JPZ (JPZ_out, \Instrução [7], \Instrução [6], ~\Instrução [5], ~\Instrução [4], clk_PC, Zero);  // AND_Gate
  nand nand_1 (nand_1_out, \Instrução [7], ~\Instrução [6], \Instrução [5]);  // NAND_Gate
  and and_5 (E, \Instrução [4], nand_1_out);

  assign \B_Endereços  = \Instrução [3:0];
  assign Dados = \Instrução [3:0];
  assign \Direção  = \Instrução [4];
  assign Operando = \Instrução [3:0];
  assign \Operação  = \Instrução [7:5];
  assign RST_PC = Reset;
endmodule
